# Fritzing sketch space-clock (saved by Fritzing 1.0.7)

parts:
  Pico/Pico2_Mod_1 = Raspberry Pi Pico or Pico 2
  D1 = Schottky Diode [part_number=1N5817 package="300 mil [THT]"]
  Adafruit_Sunken_USB_Type_C_Breakout1 = Adafruit Sunken USB Type C Breakout [mn=Adafruit mpn=#6050 part_number=#6050]
  Part1 = 0.56" 7-segment LED Backpack [part_number=1002]
  S1 = Momentary Switch [package=ksa_sealed_tac_switch]

nets:
  N1: Pico/Pico2_Mod_1.pin_6, Part1.SDA
  N2: Pico/Pico2_Mod_1.pin_7, Part1.SCL
  GND: Pico/Pico2_Mod_1.pin_8, Pico/Pico2_Mod_1.pin_28, Pico/Pico2_Mod_1.pin_38, Pico/Pico2_Mod_1.pin_42, Adafruit_Sunken_USB_Type_C_Breakout1.GND, Part1.GND, S1.4
  N3: Pico/Pico2_Mod_1.pin_26, S1.2
  N4: Pico/Pico2_Mod_1.pin_36, Part1.VDD
  N5: Pico/Pico2_Mod_1.pin_39, D1.cathode
  N6: D1.anode, Adafruit_Sunken_USB_Type_C_Breakout1.VBUS

custom parts:
  Raspberry Pi Pico or Pico 2: Raspberry Pi Pico and Pico 2. Based around the RP2040 and RP2350 microcontrollers respectively, Picos are low cost microcontroller device bringing Raspberry Pi quality, cost, and easy of use to the microcontroller space. Jan 2021, Split part in to two versions: tht (this one) and SMD. This one will drill holes for a .1 in header in pcb to allow plugging in the module as well as providing pads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
